// Logisim project cpu.circ as structural Verilog: 1 circuit, main circuit cpu
module cpu (
  input  Rest
);

  wire Clk_out, main_1_regdst, main_1_regwren;
  wire [4:0] multiplexer_1_out;
  wire [31:0] adder_1_out, InstMem_memreaddata, PC_q;

  Clock Clk (.out(Clk_out));
  Register #(.width(32)) PC (.D(adder_1_out), .en(1'b1), .clk(Clk_out), .Q(PC_q), .clr(Rest));
  Adder #(.width(32)) adder_1 (.a(32'h4), .b(PC_q), .out(adder_1_out));  // open: cin, cout
  mem InstMem (
    .MemAddress(PC_q), .clk(Clk_out), .MemReadData(InstMem_memreaddata));  // open: MemWriteMask, MemWriteData
  Multiplexer #(.width(5)) multiplexer_1 (
    .in0(InstMem_memreaddata[20:16]), .in1(InstMem_memreaddata[15:11]), .out(multiplexer_1_out),
    .sel(main_1_regdst));
  Control_main main_1 (
    .Opcode(InstMem_memreaddata[31:26]), .RegDst(main_1_regdst), .RegWrEn(main_1_regwren));  // open: Branch, Jump, AluSrc, MemToReg, AluOpr, MemWrMask
  // regfile RegisterFile: pin names not known; wires that end beside it: InstMem_memreaddata[25:21], InstMem_memreaddata[20:16], multiplexer_1_out, main_1_regwren, Clk_out, InstMem_memreaddata[5:0]
  signExtend signextend_1 (.Immd(InstMem_memreaddata[15:0]));  // open: Extended
  // mem DataMem: pin names not known
endmodule
